// Logisim project Submission.circ as structural Verilog: 1 circuit, main circuit main
module main (
  input  A0,
  input  A1,
  input  B1,
  input  B0,
  output X,
  output Y,
  output Z,
  output Q
);

  wire and_1_out, and_2_out, and_3_out, and_4_out, and_5_out, and_6_out, and_7_out, and_8_out, and_9_out,
       and_10_out, and_11_out, and_12_out, and_13_out, and_14_out, and_15_out, and_16_out, and_17_out,
       and_18_out, and_19_out, and_20_out, and_21_out, and_22_out, and_23_out, and_24_out, and_25_out,
       and_26_out, and_27_out, and_28_out, and_29_out, and_30_out, and_31_out, and_32_out, and_33_out,
       and_34_out, and_35_out, and_36_out, and_37_out, and_38_out, and_39_out, not_1_out, not_2_out,
       not_3_out, not_4_out, not_5_out, not_6_out, not_7_out, not_8_out, not_9_out, not_10_out, not_11_out,
       not_12_out, not_13_out, not_14_out, not_15_out, not_16_out, or_1_out, or_2_out, or_3_out, or_4_out,
       or_5_out, or_6_out, or_7_out, or_9_out, or_10_out, or_11_out, or_12_out, or_13_out;

  not not_1 (not_1_out, B1);
  not not_2 (not_2_out, A1);
  not not_3 (not_3_out, A0);
  and and_1 (and_1_out, A1, not_1_out);
  and and_2 (and_2_out, B1, not_7_out);
  and and_3 (and_3_out, A1, A0);
  and and_4 (and_4_out, B0, B1);
  not not_4 (not_4_out, A0);
  and and_5 (and_5_out, not_3_out, not_2_out);
  not not_5 (not_5_out, B1);
  not not_6 (not_6_out, A1);
  and and_6 (and_6_out, and_1_out, B0);
  and and_7 (and_7_out, A1, and_2_out);
  not not_7 (not_7_out, B0);
  not not_8 (not_8_out, B1);
  not not_9 (not_9_out, B1);
  and and_8 (and_8_out, A1, A0);
  and and_9 (and_9_out, B1, not_10_out);
  not not_10 (not_10_out, B0);
  and and_10 (and_10_out, not_2_out, A0);
  not not_11 (not_11_out, B1);
  and and_11 (and_11_out, not_11_out, not_12_out);
  not not_12 (not_12_out, B0);
  and and_12 (and_12_out, B0, not_2_out);
  not not_13 (not_13_out, A0);
  and and_13 (and_13_out, not_13_out, not_14_out);
  not not_14 (not_14_out, B1);
  or or_1 (or_1_out, and_6_out, and_25_out);
  not not_15 (not_15_out, B0);
  and and_14 (and_14_out, not_15_out, not_5_out);
  and and_15 (and_15_out, and_14_out, not_6_out);
  and and_16 (and_16_out, not_2_out, not_4_out);
  and and_17 (and_17_out, not_7_out, A0);
  and and_18 (and_18_out, A0, not_2_out);
  and and_19 (and_19_out, not_9_out, B0);
  and and_20 (and_20_out, A1, not_4_out);
  and and_21 (and_21_out, not_7_out, B1);
  not not_16 (not_16_out, B1);
  and and_22 (and_22_out, and_8_out, and_9_out);
  and and_23 (and_23_out, and_10_out, and_11_out);
  and and_24 (and_24_out, and_12_out, and_13_out);
  and and_25 (and_25_out, and_14_out, A1);
  or or_2 (or_2_out, and_15_out, and_31_out);
  and and_26 (and_26_out, and_3_out, and_4_out);
  and and_27 (and_27_out, A1, A0);
  and and_28 (and_28_out, B1, B0);
  and and_29 (and_29_out, and_16_out, B1);
  and and_30 (and_30_out, and_17_out, not_8_out);
  and and_31 (and_31_out, and_18_out, and_19_out);
  and and_32 (and_32_out, and_20_out, and_21_out);
  and and_33 (and_33_out, A1, not_16_out);
  and and_34 (and_34_out, and_5_out, B1);
  and and_35 (and_35_out, and_27_out, and_28_out);
  or or_3 (or_3_out, and_29_out, and_30_out);
  or or_4 (or_4_out, and_31_out, and_32_out);
  or or_5 (or_5_out, and_23_out, and_24_out);
  or or_6 (or_6_out, or_3_out, or_4_out);
  or or_7 (or_7_out, and_33_out, and_22_out);
  or or_8 (X, and_35_out, or_6_out);
  and and_36 (and_36_out, not_2_out, B1);
  and and_37 (and_37_out, not_2_out, not_9_out);
  or or_9 (or_9_out, or_7_out, or_5_out);
  and and_38 (and_38_out, and_37_out, B0);
  or or_10 (or_10_out, or_1_out, or_2_out);
  and and_39 (and_39_out, and_28_out, A1);
  or or_11 (or_11_out, or_10_out, and_7_out);
  or or_12 (or_12_out, and_36_out, and_32_out);
  or or_13 (or_13_out, and_39_out, and_38_out);
  or or_14 (Q, or_11_out, and_26_out);
  or or_15 (Y, or_12_out, or_13_out);
  or or_16 (Z, or_9_out, and_34_out);
endmodule
